// Logisim project processor.circ as structural Verilog: 10 circuits, main circuit main
module main (
);

  wire and_1_out, and_2_out, and_3_out, and_4_out, and_6_out, clock_1_out, CMP_FLAG, irdecoder_1_lit_flag,
       multiplexer_3_out, multiplexer_4_out, not_1_out, not_2_out, not_3_out, or_1_out, or_2_out, or_3_out,
       READ_MEM, RESET, rgb_video_1_p2, STAGE_EXEC, STAGE_FETCH, STAGE_MEM_READ, STAGE_STORE, STOP, undriven,
       undriven_2, USE_ALU_OUTPUT, USE_MEM_OUTPUT, WRITE_MEM, WRITE_PC, WRITE_REG, WRITE_SCR_COORD,
       WRITE_SCR_PXL;
  wire [3:0] irdecoder_1_reg1, irdecoder_1_reg2;
  wire [6:0] bitselector_1_out, bitselector_2_out;
  wire [7:0] irdecoder_1_op_code;
  wire [15:0] adder_1_out, addrdowngrader_1_addr_out, addrdowngrader_2_addr_out, multiplexer_1_out,
       multiplexer_2_out, PC_q;
  wire [23:0] bitselector_3_out;
  wire [31:0] alu_1_alu_out, IR_q, multiplexer_5_out, multiplexer_6_out, multiplexer_7_out,
       multiplexer_8_out, multiplexer_9_out, ram_1_dout, register_5_q, register_6_q, registerfile16_1_ra,
       registerfile16_1_rb, rom_1_p2, rom_1_p3;

  Clock clock_1 (.out(clock_1_out));
  Button button_1 (.out(RESET));
  LED led_1 (.in(STOP));
  and and_1 (and_1_out, WRITE_PC, CMP_FLAG);
  and and_2 (and_2_out, clock_1_out, not_1_out);
  not not_1 (not_1_out, STOP);
  Register #(.width(16)) PC (.D(multiplexer_1_out), .en(1'b1), .clk(STAGE_STORE), .Q(PC_q), .clr(RESET));
  Multiplexer #(.width(16)) multiplexer_1 (
    .in0(adder_1_out), .in1(addrdowngrader_1_addr_out), .out(multiplexer_1_out), .sel(and_1_out));
  Pull_Resistor pull_resistor_1 (.node(RESET));
  AddrDowngrader addrdowngrader_1 (.ADDR_IN(multiplexer_5_out), .ADDR_OUT(addrdowngrader_1_addr_out));
  Register #(.width(1)) register_1 (.D(or_1_out), .clk(or_2_out), .Q(STAGE_FETCH));  // open: en, clr
  or or_1 (or_1_out, RESET, STAGE_STORE);
  or or_2 (or_2_out, and_2_out, RESET);
  Adder #(.width(16)) adder_1 (.a(PC_q), .b(multiplexer_2_out), .out(adder_1_out));  // open: cin, cout
  Multiplexer #(.width(16)) multiplexer_2 (
    .in0(16'h1), .in1(16'h2), .out(multiplexer_2_out), .sel(irdecoder_1_lit_flag));
  // ROM #(.addrWidth(16), .dataWidth(32), .line("dual"), .misaligned("true")) rom_1: pin names not known; wires that end beside it: PC_q, rom_1_p2, rom_1_p3
  Register #(.width(1)) register_2 (.D(STAGE_FETCH), .clk(or_2_out), .Q(STAGE_EXEC), .clr(RESET));  // open: en
  Register #(.width(1)) register_3 (
    .D(multiplexer_3_out), .en(undriven), .clk(or_2_out), .Q(STAGE_MEM_READ));  // open: clr
  Multiplexer multiplexer_3 (.in0(1'b0), .in1(STAGE_EXEC), .out(multiplexer_3_out), .sel(READ_MEM));
  Multiplexer multiplexer_4 (.in0(STAGE_EXEC), .in1(STAGE_MEM_READ), .out(multiplexer_4_out), .sel(READ_MEM));
  Register #(.width(1)) register_4 (
    .D(multiplexer_4_out), .en(undriven_2), .clk(or_2_out), .Q(STAGE_STORE), .clr(RESET));
  Register #(.trigger("high"), .width(32)) IR (.D(rom_1_p2), .en(1'b1), .clk(STAGE_FETCH), .Q(IR_q), .clr(RESET));
  PLA #(.in_width(8), .out_width(1), .\table ("01000xxx 1 # JMP")) pla_1 (.in(irdecoder_1_op_code), .out(WRITE_PC));
  PLA #(.in_width(8), .out_width(1), .\table ("11111111 1 # stop instruction")) pla_2 (
    .in(irdecoder_1_op_code), .out(STOP));
  PLA #(.in_width(8), .out_width(1), .\table ("10000000 1 # SSET")) pla_3 (
    .in(irdecoder_1_op_code), .out(WRITE_SCR_COORD));
  PLA #(.in_width(8), .out_width(1), .\table ("00000010 1 # MOVE\n00000100 1 # LOAD\n00010xxx 1 # INT ALU\n00100xxx 1 # FLOAT ALU\n00110xxx 1 # LOGIC ALU")) pla_4 (
    .in(irdecoder_1_op_code), .out(WRITE_REG));
  PLA #(.in_width(8), .out_width(1), .\table ("10000001 1 # SOUT")) pla_5 (
    .in(irdecoder_1_op_code), .out(WRITE_SCR_PXL));
  PLA #(.in_width(8), .out_width(1), .\table ("00000011 1 # STORE")) pla_6 (.in(irdecoder_1_op_code), .out(WRITE_MEM));
  PLA #(.in_width(8), .out_width(1), .\table ("00000100 1 # LOAD")) pla_7 (.in(irdecoder_1_op_code), .out(READ_MEM));
  PLA #(.in_width(8), .out_width(1), .\table ("00000100 1 # LOAD")) pla_8 (
    .in(irdecoder_1_op_code), .out(USE_MEM_OUTPUT));
  PLA #(.in_width(8), .out_width(1), .\table ("00010xxx 1 # INT ALU\n00100xxx 1 # FLOAT ALU\n00110xxx 1 # LOGIC ALU\n00000010 1 # MOV (passthrough)")) pla_9 (
    .in(irdecoder_1_op_code), .out(USE_ALU_OUTPUT));
  IRDecoder irdecoder_1 (
    .INST(IR_q), .OP_CODE(irdecoder_1_op_code), .REG1(irdecoder_1_reg1), .REG2(irdecoder_1_reg2),
    .LIT_FLAG(irdecoder_1_lit_flag));
  and and_3 (and_3_out, STAGE_STORE, WRITE_REG);
  RegisterFile16 registerfile16_1 (
    .RA_SELECT(irdecoder_1_reg1), .RB_SELECT(irdecoder_1_reg2), .WRITE_VAL(multiplexer_8_out),
    .WRITE_STAGE(and_3_out), .RESET(RESET), .CLOCK(STAGE_EXEC), .RA(registerfile16_1_ra),
    .RB(registerfile16_1_rb));
  Multiplexer #(.width(32)) multiplexer_5 (
    .in0(registerfile16_1_rb), .in1(rom_1_p3), .out(multiplexer_5_out), .sel(irdecoder_1_lit_flag));
  or or_3 (or_3_out, STAGE_MEM_READ, STAGE_STORE);
  Register #(.width(32)) register_5 (
    .D(registerfile16_1_ra), .clk(and_4_out), .Q(register_5_q), .clr(RESET));  // open: en
  and and_4 (and_4_out, WRITE_SCR_COORD, STAGE_STORE);
  Register #(.width(32)) register_6 (
    .D(multiplexer_5_out), .clk(and_4_out), .Q(register_6_q), .clr(RESET));  // open: en
  Multiplexer #(.width(32)) multiplexer_6 (
    .in0(registerfile16_1_ra), .in1(multiplexer_5_out), .out(multiplexer_6_out), .sel(READ_MEM));
  Multiplexer #(.width(32)) multiplexer_7 (
    .in0(registerfile16_1_ra), .in1(multiplexer_5_out), .out(multiplexer_7_out), .sel(WRITE_MEM));
  RAM #(.addrWidth(16), .dataWidth(32)) ram_1 (
    .addr(addrdowngrader_2_addr_out), .we(WRITE_MEM), .clk(or_3_out), .din(multiplexer_7_out),
    .dout(ram_1_dout));  // open: oe
  AddrDowngrader addrdowngrader_2 (.ADDR_IN(multiplexer_6_out), .ADDR_OUT(addrdowngrader_2_addr_out));
  BitSelector #(.group(7), .width(32)) bitselector_1 (.in(register_5_q), .out(bitselector_1_out), .sel(3'b000));
  BitSelector #(.group(7), .width(32)) bitselector_2 (.in(register_6_q), .out(bitselector_2_out), .sel(3'b000));
  BitSelector #(.group(24), .width(32)) bitselector_3 (.in(multiplexer_5_out), .out(bitselector_3_out), .sel(1'b0));
  ALU alu_1 (
    .INPUT_1(registerfile16_1_ra), .INPUT_2(multiplexer_5_out), .CLOCK(STAGE_STORE),
    .OP_CODE(irdecoder_1_op_code), .ALU_OUT(alu_1_alu_out), .FLAG(CMP_FLAG));
  // RGB_Video rgb_video_1: pin names not known; wires that end beside it: RESET, rgb_video_1_p2, 1'b1, bitselector_1_out, bitselector_2_out, bitselector_3_out
  and and_5 (rgb_video_1_p2, WRITE_SCR_PXL, STAGE_STORE);
  Multiplexer #(.width(32)) multiplexer_8 (
    .in0(alu_1_alu_out), .in1(ram_1_dout), .out(multiplexer_8_out), .sel(USE_MEM_OUTPUT));
  Multiplexer #(.width(32)) multiplexer_9 (
    .in0(multiplexer_8_out), .in1(rom_1_p3), .out(multiplexer_9_out), .sel(and_6_out));
  and and_6 (and_6_out, not_2_out, irdecoder_1_lit_flag, not_3_out);
  not not_2 (not_2_out, USE_MEM_OUTPUT);
  not not_3 (not_3_out, USE_ALU_OUTPUT);

  // Notes on the sheet:
  //   contents of rom_1 (hex, n*v repeats v):
  //   20002 0 21002 1 100100 400002 4 ff0000
endmodule

// RRB
module RegisterFile (
  input  [31:0] WRITE_VAL,
  input  WRITE_STAGE,
  input  [3:0] RA_SELECT,
  input  [3:0] RB_SELECT,
  input  RESET,
  input  READ_STAGE,
  output [31:0] RA,
  output [31:0] RB
);

  wire demultiplexer_1_out0, demultiplexer_1_out1, demultiplexer_1_out2, demultiplexer_1_out3,
       demultiplexer_1_out4, demultiplexer_1_out5, demultiplexer_1_out6, demultiplexer_1_out7;
  wire [31:0] A_q, B_q, C_q, D_q, E_q, F_q, multiplexer_1_out, multiplexer_2_out, RBP_q, RSP_q;

  Pull_Resistor pull_resistor_1 (.node(WRITE_STAGE));
  Demultiplexer #(.enable("true"), .select(4)) demultiplexer_1 (
    .out0(demultiplexer_1_out0), .out1(demultiplexer_1_out1), .out2(demultiplexer_1_out2),
    .out3(demultiplexer_1_out3), .out4(demultiplexer_1_out4), .out5(demultiplexer_1_out5),
    .out6(demultiplexer_1_out6), .out7(demultiplexer_1_out7), .in(WRITE_STAGE), .sel(RA_SELECT));  // open: out8, out9, out10, out11, out12, out13, out14, out15, en
  Register #(.width(32)) A (.D(WRITE_VAL), .clk(demultiplexer_1_out0), .Q(A_q), .clr(RESET));  // open: en
  Register #(.width(32)) B (.D(WRITE_VAL), .clk(demultiplexer_1_out1), .Q(B_q), .clr(RESET));  // open: en
  Register #(.width(32)) C (.D(WRITE_VAL), .clk(demultiplexer_1_out2), .Q(C_q), .clr(RESET));  // open: en
  Register #(.width(32)) D (.D(WRITE_VAL), .clk(demultiplexer_1_out3), .Q(D_q), .clr(RESET));  // open: en
  Register #(.width(32)) E (.D(WRITE_VAL), .clk(demultiplexer_1_out4), .Q(E_q), .clr(RESET));  // open: en
  Register #(.width(32)) F (.D(WRITE_VAL), .clk(demultiplexer_1_out5), .Q(F_q), .clr(RESET));  // open: en
  Register #(.width(32)) RSP (.D(WRITE_VAL), .clk(demultiplexer_1_out6), .Q(RSP_q), .clr(RESET));  // open: en
  Register #(.width(32)) RBP (.D(WRITE_VAL), .clk(demultiplexer_1_out7), .Q(RBP_q), .clr(RESET));  // open: en
  Multiplexer #(.select(4), .width(32)) multiplexer_1 (
    .in0(A_q), .in1(B_q), .in2(C_q), .in3(D_q), .in4(E_q), .in5(F_q), .in6(RSP_q), .in7(RBP_q),
    .out(multiplexer_1_out), .sel(RA_SELECT));  // open: in8, in9, in10, in11, in12, in13, in14, in15
  Register #(.width(32)) RRA (.D(multiplexer_1_out), .en(1'b1), .clk(READ_STAGE), .Q(RA), .clr(RESET));
  Multiplexer #(.select(4), .width(32)) multiplexer_2 (
    .in0(A_q), .in1(B_q), .in2(C_q), .in3(D_q), .in4(E_q), .in5(F_q), .in6(RSP_q), .in7(RBP_q),
    .out(multiplexer_2_out), .sel(RB_SELECT));  // open: in8, in9, in10, in11, in12, in13, in14, in15
  Register #(.width(32)) RRB (.D(multiplexer_2_out), .en(1'b1), .clk(READ_STAGE), .Q(RB), .clr(RESET));
endmodule

module IRSelector (
  input  [23:0] IR_input,
  output [4:0] OP_code,
  output [2:0] Register1,
  output [2:0] Register2,
  output [15:0] Liter
);

  wire [5:0] bitselector_2_out;
  wire [12:0] bitselector_1_out;

  BitSelector #(.group(13), .width(24)) bitselector_1 (.in(IR_input), .out(bitselector_1_out), .sel(1'b1));
  BitSelector #(.group(6), .width(13)) bitselector_2 (.in(bitselector_1_out), .out(bitselector_2_out), .sel(2'b01));
  BitSelector #(.group(3), .width(13)) bitselector_3 (.in(bitselector_1_out), .out(Register1), .sel(3'b001));
  BitSelector #(.group(3), .width(13)) bitselector_4 (.in(bitselector_1_out), .out(Register2), .sel(3'b000));
  BitSelector #(.group(16), .width(24)) bitselector_5 (.in(IR_input), .out(Liter), .sel(1'b0));
  BitSelector #(.group(5), .width(6)) bitselector_6 (.in(bitselector_2_out), .out(OP_code), .sel(1'b0));
endmodule

module ALU (
  input  [31:0] INPUT_1,
  input  [31:0] INPUT_2,
  input  CLOCK,
  input  [7:0] OP_CODE,
  output [31:0] ALU_OUT,
  output FLAG
);

  wire comparator_1_eq, comparator_1_gt, comparator_1_lt, comparator_2_eq, comparator_2_gt, comparator_2_lt,
       fpcomparator_1_p3, fpcomparator_1_p4, fpcomparator_1_p5, multiplexer_1_out, multiplexer_2_out,
       multiplexer_3_out, not_2_out, register_1_q, register_2_q, register_3_q;
  wire [1:0] CMP_TYPE_out, pla_1_out;
  wire [2:0] bitselector_1_out, bitselector_2_out, bitselector_3_out, bitselector_4_out;
  wire [4:0] bit_extender_1_out;
  wire [31:0] adder_1_out, and_1_out, divider_1_out, fpadder_1_out, fpdivider_1_out, fpmultiplier_1_out,
       fpnegator_1_p2, fpsubtractor_1_out, fptoint_1_p2, inttofp_1_p2, multiplexer_4_out, multiplexer_5_out,
       multiplexer_6_out, multiplier_1_out, negator_1_out, not_1_out, or_1_out, shifter_1_out, shifter_2_out,
       subtractor_1_out, xor_1_out;

  Comparator #(.width(32)) comparator_1 (
    .a(INPUT_1), .b(INPUT_2), .gt(comparator_1_gt), .eq(comparator_1_eq), .lt(comparator_1_lt));
  Comparator #(.width(32)) comparator_2 (
    .a(INPUT_1), .b(INPUT_2), .gt(comparator_2_gt), .eq(comparator_2_eq), .lt(comparator_2_lt));
  // FPComparator fpcomparator_1: pin names not known; wires that end beside it: INPUT_1, INPUT_2, fpcomparator_1_p3, fpcomparator_1_p4, fpcomparator_1_p5
  Adder #(.width(32)) adder_1 (.a(INPUT_1), .b(INPUT_2), .out(adder_1_out));  // open: cin, cout
  Subtractor #(.width(32)) subtractor_1 (.a(INPUT_1), .b(INPUT_2), .out(subtractor_1_out));  // open: bin, bout
  Multiplier #(.width(32)) multiplier_1 (.a(INPUT_1), .b(INPUT_2), .out(multiplier_1_out));  // open: cin, cout
  Divider #(.width(32)) divider_1 (.a(INPUT_1), .b(INPUT_2), .out(divider_1_out));  // open: upper, rem
  Negator #(.width(32)) negator_1 (.in(INPUT_1), .out(negator_1_out));
  Bit_Extender #(.in_width(32), .out_width(5), .\type ("zero")) bit_extender_1 (.in(INPUT_2), .out(bit_extender_1_out));
  FPAdder fpadder_1 (.a(INPUT_1), .b(INPUT_2), .out(fpadder_1_out));
  FPSubtractor fpsubtractor_1 (.a(INPUT_1), .b(INPUT_2), .out(fpsubtractor_1_out));
  FPMultiplier fpmultiplier_1 (.a(INPUT_1), .b(INPUT_2), .out(fpmultiplier_1_out));
  FPDivider fpdivider_1 (.a(INPUT_1), .b(INPUT_2), .out(fpdivider_1_out));
  // FPNegator fpnegator_1: pin names not known; wires that end beside it: INPUT_1, fpnegator_1_p2
  // FPToInt #(.width(32)) fptoint_1: pin names not known; wires that end beside it: INPUT_1, fptoint_1_p2
  // IntToFP #(.width(32)) inttofp_1: pin names not known; wires that end beside it: INPUT_1, inttofp_1_p2
  assign and_1_out = INPUT_1 & INPUT_2;  // AND_Gate and_1, 32 bits wide
  assign or_1_out = INPUT_1 | INPUT_2;  // OR_Gate or_1, 32 bits wide
  assign not_1_out = ~INPUT_1;  // NOT_Gate not_1, 32 bits wide
  assign xor_1_out = INPUT_1 ^ INPUT_2;  // XOR_Gate xor_1, 32 bits wide
  PLA #(.in_width(8), .\table ("00011000 00 # CMP\n00011001 01 # UCMP\n00011010 10 # FCMP")) CMP_TYPE (
    .in(OP_CODE), .out(CMP_TYPE_out));
  Shifter #(.width(32)) shifter_1 (.in(INPUT_1), .\dist (bit_extender_1_out), .out(shifter_1_out));
  Shifter #(.shift("lr"), .width(32)) shifter_2 (.in(INPUT_1), .\dist (bit_extender_1_out), .out(shifter_2_out));
  Multiplexer #(.select(2)) multiplexer_1 (
    .in0(comparator_1_gt), .in1(comparator_2_gt), .in2(fpcomparator_1_p3), .out(multiplexer_1_out),
    .sel(CMP_TYPE_out));  // open: in3
  Multiplexer #(.select(2)) multiplexer_2 (
    .in0(comparator_1_eq), .in1(comparator_2_eq), .in2(fpcomparator_1_p4), .out(multiplexer_2_out),
    .sel(CMP_TYPE_out));  // open: in3
  Multiplexer #(.select(2)) multiplexer_3 (
    .in0(comparator_1_lt), .in1(comparator_2_lt), .in2(fpcomparator_1_p5), .out(multiplexer_3_out),
    .sel(CMP_TYPE_out));  // open: in3
  Multiplexer #(.select(3), .width(32)) multiplexer_4 (
    .in0(adder_1_out), .in1(subtractor_1_out), .in2(multiplier_1_out), .in3(divider_1_out),
    .in4(negator_1_out), .in5(shifter_1_out), .in6(shifter_2_out), .out(multiplexer_4_out),
    .sel(bitselector_1_out));  // open: in7
  BitSelector #(.group(3)) bitselector_1 (.in(OP_CODE), .out(bitselector_1_out), .sel(2'b00));
  Multiplexer #(.select(3), .width(32)) multiplexer_5 (
    .in0(fpadder_1_out), .in1(fpsubtractor_1_out), .in2(fpmultiplier_1_out), .in3(fpdivider_1_out),
    .in4(fpnegator_1_p2), .in5(fptoint_1_p2), .in6(inttofp_1_p2), .out(multiplexer_5_out),
    .sel(bitselector_2_out));  // open: in7
  BitSelector #(.group(3)) bitselector_2 (.in(OP_CODE), .out(bitselector_2_out), .sel(2'b00));
  Multiplexer #(.select(3), .width(32)) multiplexer_6 (
    .in0(and_1_out), .in1(or_1_out), .in2(not_1_out), .in3(xor_1_out), .out(multiplexer_6_out),
    .sel(bitselector_3_out));  // open: in4, in5, in6, in7
  BitSelector #(.group(3)) bitselector_3 (.in(OP_CODE), .out(bitselector_3_out), .sel(2'b00));
  Register #(.width(1)) register_1 (.D(multiplexer_1_out), .clk(CLOCK), .Q(register_1_q));  // open: en, clr
  Register #(.width(1)) register_2 (.D(multiplexer_2_out), .clk(CLOCK), .Q(register_2_q));  // open: en, clr
  Register #(.width(1)) register_3 (.D(multiplexer_3_out), .clk(CLOCK), .Q(register_3_q));  // open: en, clr
  Multiplexer #(.select(2), .width(32)) multiplexer_7 (
    .in0(INPUT_2), .in1(multiplexer_4_out), .in2(multiplexer_5_out), .in3(multiplexer_6_out), .out(ALU_OUT),
    .sel(pla_1_out));
  PLA #(.in_width(8), .\table ("0001xxxx 01 # INT\n0010xxxx 10 # FLOAT\n0011xxxx 11 # LOGIC")) pla_1 (
    .in(OP_CODE), .out(pla_1_out));
  not not_2 (not_2_out, register_2_q);
  BitSelector #(.group(3)) bitselector_4 (.in(OP_CODE), .out(bitselector_4_out), .sel(2'b00));
  Multiplexer #(.select(3)) multiplexer_8 (
    .in0(1'b1), .in1(register_2_q), .in2(not_2_out), .in3(register_1_q), .in4(register_3_q), .out(FLAG),
    .sel(bitselector_4_out));  // open: in5, in6, in7
endmodule

module Control (
  input  [7:0] OP_CODE,
  input  CLOCK
);

  wire or_1_out, or_2_out, RESET, STAGE_EXECUTE, STAGE_FETCH, STAGE_REG, USE_ALU_OUTPUT, USE_MEM_OUTPUT,
       WRITE_MEM, WRITE_REG;

  Pull_Resistor pull_resistor_1 (.node(RESET));
  or or_1 (or_1_out, RESET, STAGE_EXECUTE);
  Register #(.width(1)) register_1 (.D(or_1_out), .en(1'b1), .clk(or_2_out), .Q(STAGE_FETCH));  // open: clr
  or or_2 (or_2_out, CLOCK, RESET);
  PLA #(.in_width(8), .out_width(1), .\table ("00000010 1 # move instruction")) pla_1 (.in(OP_CODE), .out(WRITE_REG));
  PLA #(.in_width(8), .out_width(1), .\table ("00000011 1 # store instruction")) pla_2 (.in(OP_CODE), .out(WRITE_MEM));
  PLA #(.in_width(8), .out_width(1), .\table ("00000100 1 # load instruction")) pla_3 (
    .in(OP_CODE), .out(USE_MEM_OUTPUT));
  PLA pla_4 (.in(OP_CODE), .out(USE_ALU_OUTPUT));
  Register #(.width(1)) register_2 (.D(STAGE_FETCH), .en(1'b1), .clk(or_2_out), .Q(STAGE_REG), .clr(RESET));
  Register #(.width(1)) register_3 (.D(STAGE_REG), .en(1'b1), .clk(or_2_out), .Q(STAGE_EXECUTE), .clr(RESET));
endmodule

module ROMConverter (
  input  [23:0] D1,
  input  [23:0] D2,
  input  [23:0] D3,
  input  [23:0] D4,
  output [23:0] INST
);

  wire [23:0] or_1_out, or_2_out, shifter_1_out, shifter_2_out, shifter_3_out;

  Shifter #(.width(24)) shifter_1 (.in(D1), .\dist (5'b01100), .out(shifter_1_out));
  Shifter #(.width(24)) shifter_2 (.in(D2), .\dist (5'b00100), .out(shifter_2_out));
  Shifter #(.width(24)) shifter_3 (.in(D3), .\dist ({5{1'b0}}), .out(shifter_3_out));
  assign or_1_out = shifter_1_out | shifter_2_out;  // OR_Gate or_1, 24 bits wide
  assign or_2_out = shifter_3_out | D4;  // OR_Gate or_2, 24 bits wide
  assign INST = or_1_out | or_2_out;  // OR_Gate or_3, 24 bits wide
endmodule

module IRDecoder (
  input  [31:0] INST,
  output [7:0] OP_CODE,
  output [3:0] REG1,
  output [3:0] REG2,
  output LIT_FLAG
);

  BitSelector #(.group(8), .width(32)) bitselector_1 (.in(INST), .out(OP_CODE), .sel(2'b10));
  BitSelector #(.group(4), .width(32)) bitselector_2 (.in(INST), .out(REG1), .sel(3'b011));
  BitSelector #(.group(4), .width(32)) bitselector_3 (.in(INST), .out(REG2), .sel(3'b010));
  BitSelector #(.width(32)) bitselector_4 (.in(INST), .out(LIT_FLAG), .sel(5'b00001));
endmodule

module CMPFlagSelector (
  input  GR_FLAG,
  input  EQ_FLAG,
  input  SM_FLAG,
  input  [7:0] OP_CODE,
  output FLAG
);

  wire not_1_out;
  wire [2:0] bitselector_1_out;

  not not_1 (not_1_out, EQ_FLAG);
  BitSelector #(.group(3)) bitselector_1 (.in(OP_CODE), .out(bitselector_1_out), .sel(2'b00));
  Multiplexer #(.select(3)) multiplexer_1 (
    .in0(1'b1), .in1(EQ_FLAG), .in2(not_1_out), .in3(GR_FLAG), .in4(SM_FLAG), .out(FLAG),
    .sel(bitselector_1_out));  // open: in5, in6, in7
endmodule

module AddrDowngrader (
  input  [31:0] ADDR_IN,
  output [15:0] ADDR_OUT
);

  BitSelector #(.group(16), .width(32)) bitselector_1 (.in(ADDR_IN), .out(ADDR_OUT), .sel(1'b0));
endmodule

module RegisterFile16 (
  input  [3:0] RA_SELECT,
  input  [3:0] RB_SELECT,
  input  [31:0] WRITE_VAL,
  input  WRITE_STAGE,
  input  RESET,
  input  CLOCK,
  output [31:0] RA,
  output [31:0] RB
);

  wire demultiplexer_1_out0, demultiplexer_1_out1, demultiplexer_1_out2, demultiplexer_1_out3,
       demultiplexer_1_out4, demultiplexer_1_out5, demultiplexer_1_out6, demultiplexer_1_out7,
       demultiplexer_1_out14, demultiplexer_1_out15;
  wire [31:0] A_q, B_q, C_q, D_q, E_q, F_q, G_q, H_q, multiplexer_1_out, multiplexer_2_out, RBP_q, RSP_q;

  Pull_Resistor pull_resistor_1 (.node(WRITE_STAGE));
  Demultiplexer #(.enable("true"), .select(4)) demultiplexer_1 (
    .out0(demultiplexer_1_out0), .out1(demultiplexer_1_out1), .out2(demultiplexer_1_out2),
    .out3(demultiplexer_1_out3), .out4(demultiplexer_1_out4), .out5(demultiplexer_1_out5),
    .out6(demultiplexer_1_out6), .out7(demultiplexer_1_out7), .out14(demultiplexer_1_out14),
    .out15(demultiplexer_1_out15), .in(WRITE_STAGE), .sel(RA_SELECT));  // open: out8, out9, out10, out11, out12, out13, en
  Register #(.width(32)) A (.D(WRITE_VAL), .clk(demultiplexer_1_out0), .Q(A_q), .clr(RESET));  // open: en
  Register #(.width(32)) B (.D(WRITE_VAL), .clk(demultiplexer_1_out1), .Q(B_q), .clr(RESET));  // open: en
  Register #(.width(32)) C (.D(WRITE_VAL), .clk(demultiplexer_1_out2), .Q(C_q), .clr(RESET));  // open: en
  Register #(.width(32)) D (.D(WRITE_VAL), .clk(demultiplexer_1_out3), .Q(D_q), .clr(RESET));  // open: en
  Register #(.width(32)) E (.D(WRITE_VAL), .clk(demultiplexer_1_out4), .Q(E_q), .clr(RESET));  // open: en
  Register #(.width(32)) F (.D(WRITE_VAL), .clk(demultiplexer_1_out5), .Q(F_q), .clr(RESET));  // open: en
  Register #(.width(32)) G (.D(WRITE_VAL), .clk(demultiplexer_1_out6), .Q(G_q), .clr(RESET));  // open: en
  Register #(.width(32)) H (.D(WRITE_VAL), .clk(demultiplexer_1_out7), .Q(H_q), .clr(RESET));  // open: en
  Register #(.width(32)) RSP (.D(WRITE_VAL), .clk(demultiplexer_1_out14), .Q(RSP_q), .clr(RESET));  // open: en
  Register #(.width(32)) RBP (.D(WRITE_VAL), .clk(demultiplexer_1_out15), .Q(RBP_q), .clr(RESET));  // open: en
  Multiplexer #(.select(4), .width(32)) multiplexer_1 (
    .in0(A_q), .in1(B_q), .in2(C_q), .in3(D_q), .in4(E_q), .in5(F_q), .in6(G_q), .in7(H_q), .in14(RSP_q),
    .in15(RBP_q), .out(multiplexer_1_out), .sel(RA_SELECT));  // open: in8, in9, in10, in11, in12, in13
  Register #(.width(32)) register_1 (.D(multiplexer_1_out), .en(1'b1), .clk(CLOCK), .Q(RA));  // open: clr
  Multiplexer #(.select(4), .width(32)) multiplexer_2 (
    .in0(A_q), .in1(B_q), .in2(C_q), .in3(D_q), .in4(E_q), .in5(F_q), .in6(G_q), .in7(H_q), .in14(RSP_q),
    .in15(RBP_q), .out(multiplexer_2_out), .sel(RB_SELECT));  // open: in8, in9, in10, in11, in12, in13
  Register #(.width(32)) register_2 (.D(multiplexer_2_out), .en(1'b1), .clk(CLOCK), .Q(RB));  // open: clr
endmodule
